// Logisim project main.circ as structural Verilog: 6 circuits, main circuit stage1
module main (
);

  wire and_1_out, and_2_out, and_3_out, and_4_out, and_5_out, and_6_out, and_7_out, and_8_out, and_9_out,
       and_10_out, and_11_out, and_12_out, and_13_out, and_14_out, and_15_out, and_16_out, and_17_out,
       and_18_out, button_1_out, button_2_out, button_3_out, clock_1_out, d_ff_1_q, d_ff_3_q, d_ff_4_q,
       d_ff_6_q, d_ff_11_q, d_ff_12_q, d_ff_19_q, d_ff_21_q, d_ff_23_q, d_ff_25_q, j_k_ff_1_q, j_k_ff_2_q,
       j_k_ff_3_q, j_k_ff_4_q, j_k_ff_5_q, j_k_ff_6_q, j_k_ff_7_q, j_k_ff_8_q, j_k_ff_9_q, j_k_ff_10_q,
       j_k_ff_11_q, j_k_ff_12_q, j_k_ff_13_q, j_k_ff_14_q, j_k_ff_15_q, t_ff_1_q;
  wire [3:0] d_ff_2_q, d_ff_8_q, d_ff_15_q, d_ff_16_q, d_ff_32_q, d_ff_33_q, d_ff_34_q, d_ff_36_q;

  Hex_Digit_Display hex_digit_display_1 (.value(d_ff_2_q));  // open: dp
  Hex_Digit_Display hex_digit_display_2 (.value(d_ff_8_q));  // open: dp
  Button button_1 (.out(button_1_out));
  Hex_Digit_Display hex_digit_display_3 (.value(d_ff_16_q));  // open: dp
  Button button_2 (.out(button_2_out));
  Hex_Digit_Display hex_digit_display_4 (.value(d_ff_15_q));  // open: dp
  Button button_3 (.out(button_3_out));
  Hex_Digit_Display hex_digit_display_5 (.value(d_ff_36_q));  // open: dp
  LED led_1 (.in(t_ff_1_q));
  T_Flip_Flop t_ff_1 (.T(button_1_out), .clk(button_1_out), .Q(t_ff_1_q), .reset(button_3_out));  // open: Qn, preset
  Hex_Digit_Display hex_digit_display_6 (.value(d_ff_33_q));  // open: dp
  Hex_Digit_Display hex_digit_display_7 (.value(d_ff_32_q));  // open: dp
  Hex_Digit_Display hex_digit_display_8 (.value(d_ff_34_q));  // open: dp
  D_Flip_Flop d_ff_1 (.D(d_ff_23_q), .clk(clock_1_out), .Q(d_ff_1_q));  // open: Qn, preset, reset
  and and_1 (and_1_out, j_k_ff_14_q, j_k_ff_1_q);
  J_K_Flip_Flop j_k_ff_1 (
    .J(d_ff_1_q), .K(d_ff_1_q), .clk(d_ff_1_q), .Q(j_k_ff_1_q), .reset(and_17_out));  // open: Qn, preset
  D_Flip_Flop d_ff_2 (.D(j_k_ff_1_q), .clk(clock_1_out), .Q(d_ff_2_q[0]), .reset(button_3_out));  // open: Qn, preset
  and and_2 (and_2_out, and_1_out, d_ff_23_q);
  D_Flip_Flop d_ff_3 (.D(j_k_ff_1_q), .clk(d_ff_1_q), .Q(d_ff_3_q), .reset(button_3_out));  // open: Qn, preset
  D_Flip_Flop d_ff_4 (.D(and_2_out), .clk(clock_1_out), .Q(d_ff_4_q), .reset(button_3_out));  // open: Qn, preset
  and and_3 (and_3_out, j_k_ff_7_q, j_k_ff_2_q);
  and and_4 (and_4_out, j_k_ff_11_q, j_k_ff_2_q);
  J_K_Flip_Flop #(.trigger("falling")) j_k_ff_2 (
    .J(and_5_out), .K(and_5_out), .clk(clock_1_out), .Q(j_k_ff_2_q), .reset(and_3_out));  // open: Qn, preset
  D_Flip_Flop #(.trigger("falling")) d_ff_5 (
    .D(j_k_ff_2_q), .clk(clock_1_out), .Q(d_ff_15_q[3]), .reset(button_3_out));  // open: Qn, preset
  D_Flip_Flop d_ff_6 (.D(and_4_out), .clk(clock_1_out), .Q(d_ff_6_q));  // open: Qn, preset, reset
  J_K_Flip_Flop j_k_ff_3 (
    .J(d_ff_3_q), .K(d_ff_3_q), .clk(d_ff_3_q), .Q(j_k_ff_3_q), .reset(and_17_out));  // open: Qn, preset
  J_K_Flip_Flop j_k_ff_4 (
    .J(d_ff_4_q), .K(d_ff_4_q), .clk(d_ff_4_q), .Q(j_k_ff_4_q), .reset(and_18_out));  // open: Qn, preset
  and and_5 (and_5_out, and_10_out, j_k_ff_5_q);
  and and_6 (and_6_out, d_ff_6_q, j_k_ff_12_q);
  and and_7 (and_7_out, j_k_ff_8_q, j_k_ff_6_q);
  D_Flip_Flop d_ff_7 (.D(j_k_ff_3_q), .clk(clock_1_out), .Q(d_ff_2_q[1]), .reset(button_3_out));  // open: Qn, preset
  D_Flip_Flop d_ff_8 (.D(j_k_ff_4_q), .clk(clock_1_out), .Q(d_ff_8_q[0]), .reset(button_3_out));  // open: Qn, preset
  J_K_Flip_Flop #(.trigger("falling")) j_k_ff_5 (
    .J(and_10_out), .K(and_10_out), .clk(clock_1_out), .Q(j_k_ff_5_q), .reset(and_3_out));  // open: Qn, preset
  D_Flip_Flop #(.trigger("falling")) d_ff_9 (
    .D(j_k_ff_5_q), .clk(clock_1_out), .Q(d_ff_15_q[2]), .reset(button_3_out));  // open: Qn, preset
  and and_8 (and_8_out, and_6_out, j_k_ff_8_q);
  J_K_Flip_Flop #(.trigger("falling")) j_k_ff_6 (
    .J(and_8_out), .K(and_8_out), .clk(clock_1_out), .Q(j_k_ff_6_q), .reset(and_7_out));  // open: Qn, preset
  D_Flip_Flop #(.trigger("falling")) d_ff_10 (
    .D(j_k_ff_6_q), .clk(clock_1_out), .Q(d_ff_16_q[2]), .reset(button_3_out));  // open: Qn, preset
  and and_9 (and_9_out, j_k_ff_1_q, j_k_ff_3_q);
  D_Flip_Flop d_ff_11 (.D(and_9_out), .clk(d_ff_1_q), .Q(d_ff_11_q), .reset(button_3_out));  // open: Qn, preset
  D_Flip_Flop d_ff_12 (.D(j_k_ff_4_q), .clk(d_ff_4_q), .Q(d_ff_12_q), .reset(button_3_out));  // open: Qn, preset
  and and_10 (and_10_out, j_k_ff_11_q, j_k_ff_7_q);
  and and_11 (and_11_out, d_ff_6_q, j_k_ff_12_q);
  J_K_Flip_Flop #(.trigger("falling")) j_k_ff_7 (
    .J(j_k_ff_11_q), .K(j_k_ff_11_q), .clk(clock_1_out), .Q(j_k_ff_7_q), .reset(and_3_out));  // open: Qn, preset
  D_Flip_Flop #(.trigger("falling")) d_ff_13 (
    .D(j_k_ff_7_q), .clk(clock_1_out), .Q(d_ff_15_q[1]), .reset(button_3_out));  // open: Qn, preset
  J_K_Flip_Flop #(.trigger("falling")) j_k_ff_8 (
    .J(and_11_out), .K(and_11_out), .clk(clock_1_out), .Q(j_k_ff_8_q), .reset(and_7_out));  // open: Qn, preset
  D_Flip_Flop #(.trigger("falling")) d_ff_14 (
    .D(j_k_ff_8_q), .clk(clock_1_out), .Q(d_ff_16_q[1]), .reset(button_3_out));  // open: Qn, preset
  J_K_Flip_Flop j_k_ff_9 (
    .J(d_ff_11_q), .K(d_ff_11_q), .clk(d_ff_11_q), .Q(j_k_ff_9_q), .reset(and_17_out));  // open: Qn, preset
  J_K_Flip_Flop j_k_ff_10 (
    .J(d_ff_12_q), .K(d_ff_12_q), .clk(d_ff_12_q), .Q(j_k_ff_10_q), .reset(and_18_out));  // open: Qn, preset
  J_K_Flip_Flop #(.trigger("falling")) j_k_ff_11 (
    .J(t_ff_1_q), .K(t_ff_1_q), .clk(clock_1_out), .Q(j_k_ff_11_q), .reset(and_3_out));  // open: Qn, preset
  D_Flip_Flop #(.trigger("falling")) d_ff_15 (
    .D(j_k_ff_11_q), .clk(clock_1_out), .Q(d_ff_15_q[0]), .reset(button_3_out));  // open: Qn, preset
  J_K_Flip_Flop #(.trigger("falling")) j_k_ff_12 (
    .J(d_ff_6_q), .K(d_ff_6_q), .clk(clock_1_out), .Q(j_k_ff_12_q), .reset(and_7_out));  // open: Qn, preset
  D_Flip_Flop #(.trigger("falling")) d_ff_16 (
    .D(j_k_ff_12_q), .clk(clock_1_out), .Q(d_ff_16_q[0]), .reset(button_3_out));  // open: Qn, preset
  D_Flip_Flop d_ff_17 (.D(j_k_ff_9_q), .clk(clock_1_out), .Q(d_ff_2_q[2]), .reset(button_3_out));  // open: Qn, preset
  D_Flip_Flop d_ff_18 (.D(j_k_ff_10_q), .clk(clock_1_out), .Q(d_ff_8_q[1]), .reset(button_3_out));  // open: Qn, preset
  and and_12 (and_12_out, j_k_ff_1_q, j_k_ff_3_q, j_k_ff_9_q);
  and and_13 (and_13_out, j_k_ff_4_q, j_k_ff_10_q);
  D_Flip_Flop d_ff_19 (.D(and_13_out), .clk(d_ff_4_q), .Q(d_ff_19_q), .reset(button_3_out));  // open: Qn, preset
  Clock clock_1 (.out(clock_1_out));
  D_Flip_Flop #(.trigger("falling")) d_ff_20 (
    .D(clock_1_out), .clk(clock_1_out), .Q(d_ff_16_q[3]), .reset(button_3_out));  // open: Qn, preset
  D_Flip_Flop d_ff_21 (.D(and_12_out), .clk(d_ff_1_q), .Q(d_ff_21_q), .reset(button_3_out));  // open: Qn, preset
  J_K_Flip_Flop j_k_ff_13 (
    .J(d_ff_19_q), .K(d_ff_19_q), .clk(d_ff_19_q), .Q(j_k_ff_13_q), .reset(and_18_out));  // open: Qn, preset
  and and_14 (and_14_out, j_k_ff_6_q, j_k_ff_12_q);
  J_K_Flip_Flop j_k_ff_14 (
    .J(d_ff_21_q), .K(d_ff_21_q), .clk(d_ff_21_q), .Q(j_k_ff_14_q), .reset(and_17_out));  // open: Qn, preset
  D_Flip_Flop d_ff_22 (.D(j_k_ff_13_q), .clk(clock_1_out), .Q(d_ff_8_q[2]), .reset(button_3_out));  // open: Qn, preset
  D_Flip_Flop #(.trigger("falling")) d_ff_23 (
    .D(and_15_out), .clk(clock_1_out), .Q(d_ff_23_q));  // open: Qn, preset, reset
  and and_15 (and_15_out, d_ff_6_q, and_14_out);
  D_Flip_Flop d_ff_24 (.D(j_k_ff_14_q), .clk(clock_1_out), .Q(d_ff_2_q[3]), .reset(button_3_out));  // open: Qn, preset
  and and_16 (and_16_out, j_k_ff_4_q, j_k_ff_10_q, j_k_ff_13_q);
  D_Flip_Flop d_ff_25 (.D(and_16_out), .clk(d_ff_4_q), .Q(d_ff_25_q), .reset(button_3_out));  // open: Qn, preset
  and and_17 (and_17_out, j_k_ff_14_q, j_k_ff_3_q);
  D_Flip_Flop #(.trigger("falling")) d_ff_26 (
    .D(d_ff_15_q[3]), .clk(button_2_out), .Q(d_ff_34_q[3]), .reset(button_3_out));  // open: Qn, preset
  D_Flip_Flop #(.trigger("falling")) d_ff_27 (
    .D(d_ff_16_q[2]), .clk(button_2_out), .Q(d_ff_32_q[2]), .reset(button_3_out));  // open: Qn, preset
  J_K_Flip_Flop j_k_ff_15 (
    .J(d_ff_25_q), .K(d_ff_25_q), .clk(d_ff_25_q), .Q(j_k_ff_15_q), .reset(and_18_out));  // open: Qn, preset
  D_Flip_Flop #(.trigger("falling")) d_ff_28 (
    .D(d_ff_15_q[2]), .clk(button_2_out), .Q(d_ff_34_q[2]), .reset(button_3_out));  // open: Qn, preset
  D_Flip_Flop #(.trigger("falling")) d_ff_29 (
    .D(d_ff_16_q[1]), .clk(button_2_out), .Q(d_ff_32_q[1]), .reset(button_3_out));  // open: Qn, preset
  and and_18 (and_18_out, j_k_ff_15_q, j_k_ff_10_q);
  D_Flip_Flop d_ff_30 (.D(j_k_ff_15_q), .clk(clock_1_out), .Q(d_ff_8_q[3]), .reset(button_3_out));  // open: Qn, preset
  D_Flip_Flop #(.trigger("falling")) d_ff_31 (
    .D(d_ff_15_q[1]), .clk(button_2_out), .Q(d_ff_34_q[1]), .reset(button_3_out));  // open: Qn, preset
  D_Flip_Flop #(.trigger("falling")) d_ff_32 (
    .D(d_ff_16_q[0]), .clk(button_2_out), .Q(d_ff_32_q[0]), .reset(button_3_out));  // open: Qn, preset
  D_Flip_Flop d_ff_33 (
    .D(d_ff_2_q[0]), .clk(button_2_out), .Q(d_ff_33_q[0]), .reset(button_3_out));  // open: Qn, preset
  D_Flip_Flop #(.trigger("falling")) d_ff_34 (
    .D(d_ff_15_q[0]), .clk(button_2_out), .Q(d_ff_34_q[0]), .reset(button_3_out));  // open: Qn, preset
  D_Flip_Flop d_ff_35 (
    .D(d_ff_16_q[3]), .clk(button_2_out), .Q(d_ff_32_q[3]), .reset(button_3_out));  // open: Qn, preset
  D_Flip_Flop d_ff_36 (
    .D(d_ff_8_q[0]), .clk(button_2_out), .Q(d_ff_36_q[0]), .reset(button_3_out));  // open: Qn, preset
  D_Flip_Flop d_ff_37 (
    .D(d_ff_2_q[1]), .clk(button_2_out), .Q(d_ff_33_q[1]), .reset(button_3_out));  // open: Qn, preset
  D_Flip_Flop d_ff_38 (
    .D(d_ff_8_q[1]), .clk(button_2_out), .Q(d_ff_36_q[1]), .reset(button_3_out));  // open: Qn, preset
  D_Flip_Flop d_ff_39 (
    .D(d_ff_2_q[2]), .clk(button_2_out), .Q(d_ff_33_q[2]), .reset(button_3_out));  // open: Qn, preset
  D_Flip_Flop d_ff_40 (
    .D(d_ff_8_q[2]), .clk(button_2_out), .Q(d_ff_36_q[2]), .reset(button_3_out));  // open: Qn, preset
  D_Flip_Flop d_ff_41 (
    .D(d_ff_2_q[3]), .clk(button_2_out), .Q(d_ff_33_q[3]), .reset(button_3_out));  // open: Qn, preset
  D_Flip_Flop d_ff_42 (
    .D(d_ff_8_q[3]), .clk(button_2_out), .Q(d_ff_36_q[3]), .reset(button_3_out));  // open: Qn, preset

  // Notes on the sheet:
  //   Minutes
  //   Start / Stop
  //   Elapsed Time
  //   Seconds
  //   :
  //   Split
  //   Reset
  //   Minutes
  //   Clock Started
  //   Split Time
  //   :
  //   Seconds
endmodule

module stage1 (
);

  wire button_1_out, t_ff_1_q;

  Hex_Digit_Display hex_digit_display_1 ();  // open: value, dp
  Hex_Digit_Display hex_digit_display_2 ();  // open: value, dp
  Button button_1 (.out(button_1_out));
  Hex_Digit_Display hex_digit_display_3 ();  // open: value, dp
  Button button_2 ();  // open: out
  Hex_Digit_Display hex_digit_display_4 ();  // open: value, dp
  Button button_3 ();  // open: out
  T_Flip_Flop t_ff_1 (.T(button_1_out), .clk(button_1_out), .Q(t_ff_1_q));  // open: Qn, reset, preset
  Hex_Digit_Display hex_digit_display_5 ();  // open: value, dp
  LED led_1 (.in(t_ff_1_q));
  Hex_Digit_Display hex_digit_display_6 ();  // open: value, dp
  Hex_Digit_Display hex_digit_display_7 ();  // open: value, dp
  Hex_Digit_Display hex_digit_display_8 ();  // open: value, dp

  // Notes on the sheet:
  //   Minutes
  //   Start / Stop
  //   Elapsed Time
  //   Seconds
  //   :
  //   Split
  //   Reset
  //   Minutes
  //   Clock Started
  //   Split Time
  //   :
  //   Seconds
endmodule

module stage2 (
);

  wire and_1_out, and_2_out, and_3_out, button_1_out, clock_1_out, j_k_ff_1_q, j_k_ff_2_q, j_k_ff_3_q,
       j_k_ff_4_q, t_ff_1_q;
  wire [3:0] d_ff_4_q;

  Hex_Digit_Display hex_digit_display_1 ();  // open: value, dp
  Hex_Digit_Display hex_digit_display_2 ();  // open: value, dp
  Button button_1 (.out(button_1_out));
  Hex_Digit_Display hex_digit_display_3 ();  // open: value, dp
  Button button_2 ();  // open: out
  Hex_Digit_Display hex_digit_display_4 (.value(d_ff_4_q));  // open: dp
  Button button_3 ();  // open: out
  Hex_Digit_Display hex_digit_display_5 ();  // open: value, dp
  LED led_1 (.in(t_ff_1_q));
  T_Flip_Flop t_ff_1 (.T(button_1_out), .clk(button_1_out), .Q(t_ff_1_q));  // open: Qn, reset, preset
  Hex_Digit_Display hex_digit_display_6 ();  // open: value, dp
  Hex_Digit_Display hex_digit_display_7 ();  // open: value, dp
  Hex_Digit_Display hex_digit_display_8 ();  // open: value, dp
  and and_1 (and_1_out, j_k_ff_3_q, j_k_ff_1_q);
  and and_2 (and_2_out, and_3_out, j_k_ff_2_q);
  J_K_Flip_Flop #(.trigger("falling")) j_k_ff_1 (
    .J(and_2_out), .K(and_2_out), .clk(clock_1_out), .Q(j_k_ff_1_q), .reset(and_1_out));  // open: Qn, preset
  D_Flip_Flop #(.trigger("falling")) d_ff_1 (
    .D(j_k_ff_1_q), .clk(clock_1_out), .Q(d_ff_4_q[3]));  // open: Qn, preset, reset
  and and_3 (and_3_out, j_k_ff_4_q, j_k_ff_3_q);
  J_K_Flip_Flop #(.trigger("falling")) j_k_ff_2 (
    .J(and_3_out), .K(and_3_out), .clk(clock_1_out), .Q(j_k_ff_2_q), .reset(and_1_out));  // open: Qn, preset
  D_Flip_Flop #(.trigger("falling")) d_ff_2 (
    .D(j_k_ff_2_q), .clk(clock_1_out), .Q(d_ff_4_q[2]));  // open: Qn, preset, reset
  J_K_Flip_Flop #(.trigger("falling")) j_k_ff_3 (
    .J(j_k_ff_4_q), .K(j_k_ff_4_q), .clk(clock_1_out), .Q(j_k_ff_3_q), .reset(and_1_out));  // open: Qn, preset
  D_Flip_Flop #(.trigger("falling")) d_ff_3 (
    .D(j_k_ff_3_q), .clk(clock_1_out), .Q(d_ff_4_q[1]));  // open: Qn, preset, reset
  J_K_Flip_Flop #(.trigger("falling")) j_k_ff_4 (
    .J(t_ff_1_q), .K(t_ff_1_q), .clk(clock_1_out), .Q(j_k_ff_4_q), .reset(and_1_out));  // open: Qn, preset
  D_Flip_Flop #(.trigger("falling")) d_ff_4 (
    .D(j_k_ff_4_q), .clk(clock_1_out), .Q(d_ff_4_q[0]));  // open: Qn, preset, reset
  Clock clock_1 (.out(clock_1_out));

  // Notes on the sheet:
  //   Minutes
  //   Start / Stop
  //   Elapsed Time
  //   Seconds
  //   :
  //   Split
  //   Reset
  //   Minutes
  //   Clock Started
  //   Split Time
  //   :
  //   Seconds
endmodule

module stage3 (
);

  wire and_1_out, and_2_out, and_3_out, and_4_out, and_5_out, and_6_out, and_7_out, and_8_out, button_1_out,
       button_3_out, clock_1_out, d_ff_2_q, j_k_ff_1_q, j_k_ff_2_q, j_k_ff_3_q, j_k_ff_4_q, j_k_ff_5_q,
       j_k_ff_6_q, j_k_ff_7_q, t_ff_1_q;
  wire [3:0] d_ff_7_q, d_ff_8_q;

  Hex_Digit_Display hex_digit_display_1 ();  // open: value, dp
  Hex_Digit_Display hex_digit_display_2 ();  // open: value, dp
  Button button_1 (.out(button_1_out));
  Hex_Digit_Display hex_digit_display_3 (.value(d_ff_8_q));  // open: dp
  Button button_2 ();  // open: out
  Hex_Digit_Display hex_digit_display_4 (.value(d_ff_7_q));  // open: dp
  Button button_3 (.out(button_3_out));
  Hex_Digit_Display hex_digit_display_5 ();  // open: value, dp
  LED led_1 (.in(t_ff_1_q));
  T_Flip_Flop t_ff_1 (.T(button_1_out), .clk(button_1_out), .Q(t_ff_1_q), .reset(button_3_out));  // open: Qn, preset
  Hex_Digit_Display hex_digit_display_6 ();  // open: value, dp
  Hex_Digit_Display hex_digit_display_7 ();  // open: value, dp
  Hex_Digit_Display hex_digit_display_8 ();  // open: value, dp
  and and_1 (and_1_out, j_k_ff_4_q, j_k_ff_1_q);
  and and_2 (and_2_out, j_k_ff_6_q, j_k_ff_1_q);
  J_K_Flip_Flop #(.trigger("falling")) j_k_ff_1 (
    .J(and_3_out), .K(and_3_out), .clk(clock_1_out), .Q(j_k_ff_1_q), .reset(and_1_out));  // open: Qn, preset
  D_Flip_Flop #(.trigger("falling")) d_ff_1 (
    .D(j_k_ff_1_q), .clk(clock_1_out), .Q(d_ff_7_q[3]), .reset(button_3_out));  // open: Qn, preset
  D_Flip_Flop d_ff_2 (.D(and_2_out), .clk(clock_1_out), .Q(d_ff_2_q), .reset(button_3_out));  // open: Qn, preset
  and and_3 (and_3_out, and_7_out, j_k_ff_2_q);
  and and_4 (and_4_out, d_ff_2_q, j_k_ff_7_q);
  and and_5 (and_5_out, j_k_ff_5_q, j_k_ff_3_q);
  J_K_Flip_Flop #(.trigger("falling")) j_k_ff_2 (
    .J(and_7_out), .K(and_7_out), .clk(clock_1_out), .Q(j_k_ff_2_q), .reset(and_1_out));  // open: Qn, preset
  D_Flip_Flop #(.trigger("falling")) d_ff_3 (
    .D(j_k_ff_2_q), .clk(clock_1_out), .Q(d_ff_7_q[2]), .reset(button_3_out));  // open: Qn, preset
  and and_6 (and_6_out, and_4_out, j_k_ff_5_q);
  J_K_Flip_Flop #(.trigger("falling")) j_k_ff_3 (
    .J(and_6_out), .K(and_6_out), .clk(clock_1_out), .Q(j_k_ff_3_q), .reset(and_5_out));  // open: Qn, preset
  D_Flip_Flop #(.trigger("falling")) d_ff_4 (
    .D(j_k_ff_3_q), .clk(clock_1_out), .Q(d_ff_8_q[2]), .reset(button_3_out));  // open: Qn, preset
  and and_7 (and_7_out, j_k_ff_6_q, j_k_ff_4_q);
  and and_8 (and_8_out, d_ff_2_q, j_k_ff_7_q);
  J_K_Flip_Flop #(.trigger("falling")) j_k_ff_4 (
    .J(j_k_ff_6_q), .K(j_k_ff_6_q), .clk(clock_1_out), .Q(j_k_ff_4_q), .reset(and_1_out));  // open: Qn, preset
  D_Flip_Flop #(.trigger("falling")) d_ff_5 (
    .D(j_k_ff_4_q), .clk(clock_1_out), .Q(d_ff_7_q[1]), .reset(button_3_out));  // open: Qn, preset
  J_K_Flip_Flop #(.trigger("falling")) j_k_ff_5 (
    .J(and_8_out), .K(and_8_out), .clk(clock_1_out), .Q(j_k_ff_5_q), .reset(and_5_out));  // open: Qn, preset
  D_Flip_Flop #(.trigger("falling")) d_ff_6 (
    .D(j_k_ff_5_q), .clk(clock_1_out), .Q(d_ff_8_q[1]), .reset(button_3_out));  // open: Qn, preset
  J_K_Flip_Flop #(.trigger("falling")) j_k_ff_6 (
    .J(t_ff_1_q), .K(t_ff_1_q), .clk(clock_1_out), .Q(j_k_ff_6_q), .reset(and_1_out));  // open: Qn, preset
  D_Flip_Flop #(.trigger("falling")) d_ff_7 (
    .D(j_k_ff_6_q), .clk(clock_1_out), .Q(d_ff_7_q[0]), .reset(button_3_out));  // open: Qn, preset
  J_K_Flip_Flop #(.trigger("falling")) j_k_ff_7 (
    .J(d_ff_2_q), .K(d_ff_2_q), .clk(clock_1_out), .Q(j_k_ff_7_q), .reset(and_5_out));  // open: Qn, preset
  D_Flip_Flop #(.trigger("falling")) d_ff_8 (
    .D(j_k_ff_7_q), .clk(clock_1_out), .Q(d_ff_8_q[0]), .reset(button_3_out));  // open: Qn, preset
  Clock clock_1 (.out(clock_1_out));
  D_Flip_Flop #(.trigger("falling")) d_ff_9 (
    .D(clock_1_out), .clk(clock_1_out), .Q(d_ff_8_q[3]), .reset(button_3_out));  // open: Qn, preset

  // Notes on the sheet:
  //   Minutes
  //   Start / Stop
  //   Elapsed Time
  //   Seconds
  //   :
  //   Split
  //   Reset
  //   Minutes
  //   Clock Started
  //   Split Time
  //   :
  //   Seconds
endmodule

module stage4 (
);

  wire and_1_out, and_2_out, and_3_out, and_4_out, and_5_out, and_6_out, and_7_out, and_8_out, and_9_out,
       and_10_out, and_11_out, and_12_out, and_13_out, and_14_out, and_15_out, and_16_out, and_17_out,
       and_18_out, button_1_out, button_3_out, clock_1_out, d_ff_1_q, d_ff_3_q, d_ff_4_q, d_ff_6_q,
       d_ff_11_q, d_ff_12_q, d_ff_19_q, d_ff_21_q, d_ff_23_q, d_ff_25_q, j_k_ff_1_q, j_k_ff_2_q, j_k_ff_3_q,
       j_k_ff_4_q, j_k_ff_5_q, j_k_ff_6_q, j_k_ff_7_q, j_k_ff_8_q, j_k_ff_9_q, j_k_ff_10_q, j_k_ff_11_q,
       j_k_ff_12_q, j_k_ff_13_q, j_k_ff_14_q, j_k_ff_15_q, t_ff_1_q;
  wire [3:0] d_ff_2_q, d_ff_8_q, d_ff_15_q, d_ff_16_q;

  Hex_Digit_Display hex_digit_display_1 (.value(d_ff_2_q));  // open: dp
  Hex_Digit_Display hex_digit_display_2 (.value(d_ff_8_q));  // open: dp
  Button button_1 (.out(button_1_out));
  Hex_Digit_Display hex_digit_display_3 (.value(d_ff_16_q));  // open: dp
  Button button_2 ();  // open: out
  Hex_Digit_Display hex_digit_display_4 (.value(d_ff_15_q));  // open: dp
  Button button_3 (.out(button_3_out));
  Hex_Digit_Display hex_digit_display_5 ();  // open: value, dp
  LED led_1 (.in(t_ff_1_q));
  T_Flip_Flop t_ff_1 (.T(button_1_out), .clk(button_1_out), .Q(t_ff_1_q), .reset(button_3_out));  // open: Qn, preset
  Hex_Digit_Display hex_digit_display_6 ();  // open: value, dp
  Hex_Digit_Display hex_digit_display_7 ();  // open: value, dp
  Hex_Digit_Display hex_digit_display_8 ();  // open: value, dp
  D_Flip_Flop d_ff_1 (.D(d_ff_23_q), .clk(clock_1_out), .Q(d_ff_1_q));  // open: Qn, preset, reset
  and and_1 (and_1_out, j_k_ff_14_q, j_k_ff_1_q);
  J_K_Flip_Flop j_k_ff_1 (
    .J(d_ff_1_q), .K(d_ff_1_q), .clk(d_ff_1_q), .Q(j_k_ff_1_q), .reset(and_17_out));  // open: Qn, preset
  D_Flip_Flop d_ff_2 (.D(j_k_ff_1_q), .clk(clock_1_out), .Q(d_ff_2_q[0]), .reset(button_3_out));  // open: Qn, preset
  and and_2 (and_2_out, and_1_out, d_ff_23_q);
  D_Flip_Flop d_ff_3 (.D(j_k_ff_1_q), .clk(d_ff_1_q), .Q(d_ff_3_q), .reset(button_3_out));  // open: Qn, preset
  D_Flip_Flop d_ff_4 (.D(and_2_out), .clk(clock_1_out), .Q(d_ff_4_q), .reset(button_3_out));  // open: Qn, preset
  and and_3 (and_3_out, j_k_ff_7_q, j_k_ff_2_q);
  and and_4 (and_4_out, j_k_ff_11_q, j_k_ff_2_q);
  J_K_Flip_Flop #(.trigger("falling")) j_k_ff_2 (
    .J(and_5_out), .K(and_5_out), .clk(clock_1_out), .Q(j_k_ff_2_q), .reset(and_3_out));  // open: Qn, preset
  D_Flip_Flop #(.trigger("falling")) d_ff_5 (
    .D(j_k_ff_2_q), .clk(clock_1_out), .Q(d_ff_15_q[3]), .reset(button_3_out));  // open: Qn, preset
  D_Flip_Flop d_ff_6 (.D(and_4_out), .clk(clock_1_out), .Q(d_ff_6_q));  // open: Qn, preset, reset
  J_K_Flip_Flop j_k_ff_3 (
    .J(d_ff_3_q), .K(d_ff_3_q), .clk(d_ff_3_q), .Q(j_k_ff_3_q), .reset(and_17_out));  // open: Qn, preset
  J_K_Flip_Flop j_k_ff_4 (
    .J(d_ff_4_q), .K(d_ff_4_q), .clk(d_ff_4_q), .Q(j_k_ff_4_q), .reset(and_18_out));  // open: Qn, preset
  and and_5 (and_5_out, and_10_out, j_k_ff_5_q);
  and and_6 (and_6_out, d_ff_6_q, j_k_ff_12_q);
  and and_7 (and_7_out, j_k_ff_8_q, j_k_ff_6_q);
  D_Flip_Flop d_ff_7 (.D(j_k_ff_3_q), .clk(clock_1_out), .Q(d_ff_2_q[1]), .reset(button_3_out));  // open: Qn, preset
  D_Flip_Flop d_ff_8 (.D(j_k_ff_4_q), .clk(clock_1_out), .Q(d_ff_8_q[0]), .reset(button_3_out));  // open: Qn, preset
  J_K_Flip_Flop #(.trigger("falling")) j_k_ff_5 (
    .J(and_10_out), .K(and_10_out), .clk(clock_1_out), .Q(j_k_ff_5_q), .reset(and_3_out));  // open: Qn, preset
  D_Flip_Flop #(.trigger("falling")) d_ff_9 (
    .D(j_k_ff_5_q), .clk(clock_1_out), .Q(d_ff_15_q[2]), .reset(button_3_out));  // open: Qn, preset
  and and_8 (and_8_out, and_6_out, j_k_ff_8_q);
  J_K_Flip_Flop #(.trigger("falling")) j_k_ff_6 (
    .J(and_8_out), .K(and_8_out), .clk(clock_1_out), .Q(j_k_ff_6_q), .reset(and_7_out));  // open: Qn, preset
  D_Flip_Flop #(.trigger("falling")) d_ff_10 (
    .D(j_k_ff_6_q), .clk(clock_1_out), .Q(d_ff_16_q[2]), .reset(button_3_out));  // open: Qn, preset
  and and_9 (and_9_out, j_k_ff_1_q, j_k_ff_3_q);
  D_Flip_Flop d_ff_11 (.D(and_9_out), .clk(d_ff_1_q), .Q(d_ff_11_q), .reset(button_3_out));  // open: Qn, preset
  D_Flip_Flop d_ff_12 (.D(j_k_ff_4_q), .clk(d_ff_4_q), .Q(d_ff_12_q), .reset(button_3_out));  // open: Qn, preset
  and and_10 (and_10_out, j_k_ff_11_q, j_k_ff_7_q);
  and and_11 (and_11_out, d_ff_6_q, j_k_ff_12_q);
  J_K_Flip_Flop #(.trigger("falling")) j_k_ff_7 (
    .J(j_k_ff_11_q), .K(j_k_ff_11_q), .clk(clock_1_out), .Q(j_k_ff_7_q), .reset(and_3_out));  // open: Qn, preset
  D_Flip_Flop #(.trigger("falling")) d_ff_13 (
    .D(j_k_ff_7_q), .clk(clock_1_out), .Q(d_ff_15_q[1]), .reset(button_3_out));  // open: Qn, preset
  J_K_Flip_Flop #(.trigger("falling")) j_k_ff_8 (
    .J(and_11_out), .K(and_11_out), .clk(clock_1_out), .Q(j_k_ff_8_q), .reset(and_7_out));  // open: Qn, preset
  D_Flip_Flop #(.trigger("falling")) d_ff_14 (
    .D(j_k_ff_8_q), .clk(clock_1_out), .Q(d_ff_16_q[1]), .reset(button_3_out));  // open: Qn, preset
  J_K_Flip_Flop j_k_ff_9 (
    .J(d_ff_11_q), .K(d_ff_11_q), .clk(d_ff_11_q), .Q(j_k_ff_9_q), .reset(and_17_out));  // open: Qn, preset
  J_K_Flip_Flop j_k_ff_10 (
    .J(d_ff_12_q), .K(d_ff_12_q), .clk(d_ff_12_q), .Q(j_k_ff_10_q), .reset(and_18_out));  // open: Qn, preset
  J_K_Flip_Flop #(.trigger("falling")) j_k_ff_11 (
    .J(t_ff_1_q), .K(t_ff_1_q), .clk(clock_1_out), .Q(j_k_ff_11_q), .reset(and_3_out));  // open: Qn, preset
  D_Flip_Flop #(.trigger("falling")) d_ff_15 (
    .D(j_k_ff_11_q), .clk(clock_1_out), .Q(d_ff_15_q[0]), .reset(button_3_out));  // open: Qn, preset
  J_K_Flip_Flop #(.trigger("falling")) j_k_ff_12 (
    .J(d_ff_6_q), .K(d_ff_6_q), .clk(clock_1_out), .Q(j_k_ff_12_q), .reset(and_7_out));  // open: Qn, preset
  D_Flip_Flop #(.trigger("falling")) d_ff_16 (
    .D(j_k_ff_12_q), .clk(clock_1_out), .Q(d_ff_16_q[0]), .reset(button_3_out));  // open: Qn, preset
  D_Flip_Flop d_ff_17 (.D(j_k_ff_9_q), .clk(clock_1_out), .Q(d_ff_2_q[2]), .reset(button_3_out));  // open: Qn, preset
  D_Flip_Flop d_ff_18 (.D(j_k_ff_10_q), .clk(clock_1_out), .Q(d_ff_8_q[1]), .reset(button_3_out));  // open: Qn, preset
  and and_12 (and_12_out, j_k_ff_1_q, j_k_ff_3_q, j_k_ff_9_q);
  and and_13 (and_13_out, j_k_ff_4_q, j_k_ff_10_q);
  D_Flip_Flop d_ff_19 (.D(and_13_out), .clk(d_ff_4_q), .Q(d_ff_19_q), .reset(button_3_out));  // open: Qn, preset
  Clock clock_1 (.out(clock_1_out));
  D_Flip_Flop #(.trigger("falling")) d_ff_20 (
    .D(clock_1_out), .clk(clock_1_out), .Q(d_ff_16_q[3]), .reset(button_3_out));  // open: Qn, preset
  D_Flip_Flop d_ff_21 (.D(and_12_out), .clk(d_ff_1_q), .Q(d_ff_21_q), .reset(button_3_out));  // open: Qn, preset
  J_K_Flip_Flop j_k_ff_13 (
    .J(d_ff_19_q), .K(d_ff_19_q), .clk(d_ff_19_q), .Q(j_k_ff_13_q), .reset(and_18_out));  // open: Qn, preset
  and and_14 (and_14_out, j_k_ff_6_q, j_k_ff_12_q);
  J_K_Flip_Flop j_k_ff_14 (
    .J(d_ff_21_q), .K(d_ff_21_q), .clk(d_ff_21_q), .Q(j_k_ff_14_q), .reset(and_17_out));  // open: Qn, preset
  D_Flip_Flop d_ff_22 (.D(j_k_ff_13_q), .clk(clock_1_out), .Q(d_ff_8_q[2]), .reset(button_3_out));  // open: Qn, preset
  D_Flip_Flop #(.trigger("falling")) d_ff_23 (
    .D(and_15_out), .clk(clock_1_out), .Q(d_ff_23_q));  // open: Qn, preset, reset
  and and_15 (and_15_out, d_ff_6_q, and_14_out);
  D_Flip_Flop d_ff_24 (.D(j_k_ff_14_q), .clk(clock_1_out), .Q(d_ff_2_q[3]), .reset(button_3_out));  // open: Qn, preset
  and and_16 (and_16_out, j_k_ff_4_q, j_k_ff_10_q, j_k_ff_13_q);
  D_Flip_Flop d_ff_25 (.D(and_16_out), .clk(d_ff_4_q), .Q(d_ff_25_q), .reset(button_3_out));  // open: Qn, preset
  and and_17 (and_17_out, j_k_ff_14_q, j_k_ff_3_q);
  J_K_Flip_Flop j_k_ff_15 (
    .J(d_ff_25_q), .K(d_ff_25_q), .clk(d_ff_25_q), .Q(j_k_ff_15_q), .reset(and_18_out));  // open: Qn, preset
  and and_18 (and_18_out, j_k_ff_15_q, j_k_ff_10_q);
  D_Flip_Flop d_ff_26 (.D(j_k_ff_15_q), .clk(clock_1_out), .Q(d_ff_8_q[3]), .reset(button_3_out));  // open: Qn, preset

  // Notes on the sheet:
  //   Minutes
  //   Start / Stop
  //   Elapsed Time
  //   Seconds
  //   :
  //   Split
  //   Reset
  //   Minutes
  //   Clock Started
  //   Split Time
  //   :
  //   Seconds
endmodule

module stage5 (
);

  wire and_1_out, and_2_out, and_3_out, and_4_out, and_5_out, and_6_out, and_7_out, and_8_out, and_9_out,
       and_10_out, and_11_out, and_12_out, and_13_out, and_14_out, and_15_out, and_16_out, and_17_out,
       and_18_out, button_1_out, button_2_out, button_3_out, clock_1_out, d_ff_1_q, d_ff_3_q, d_ff_4_q,
       d_ff_6_q, d_ff_11_q, d_ff_12_q, d_ff_19_q, d_ff_21_q, d_ff_23_q, d_ff_25_q, j_k_ff_1_q, j_k_ff_2_q,
       j_k_ff_3_q, j_k_ff_4_q, j_k_ff_5_q, j_k_ff_6_q, j_k_ff_7_q, j_k_ff_8_q, j_k_ff_9_q, j_k_ff_10_q,
       j_k_ff_11_q, j_k_ff_12_q, j_k_ff_13_q, j_k_ff_14_q, j_k_ff_15_q, t_ff_1_q;
  wire [3:0] d_ff_2_q, d_ff_8_q, d_ff_15_q, d_ff_16_q, d_ff_32_q, d_ff_33_q, d_ff_34_q, d_ff_36_q;

  Hex_Digit_Display hex_digit_display_1 (.value(d_ff_2_q));  // open: dp
  Hex_Digit_Display hex_digit_display_2 (.value(d_ff_8_q));  // open: dp
  Button button_1 (.out(button_1_out));
  Hex_Digit_Display hex_digit_display_3 (.value(d_ff_16_q));  // open: dp
  Button button_2 (.out(button_2_out));
  Hex_Digit_Display hex_digit_display_4 (.value(d_ff_15_q));  // open: dp
  Button button_3 (.out(button_3_out));
  Hex_Digit_Display hex_digit_display_5 (.value(d_ff_36_q));  // open: dp
  LED led_1 (.in(t_ff_1_q));
  T_Flip_Flop t_ff_1 (.T(button_1_out), .clk(button_1_out), .Q(t_ff_1_q), .reset(button_3_out));  // open: Qn, preset
  Hex_Digit_Display hex_digit_display_6 (.value(d_ff_33_q));  // open: dp
  Hex_Digit_Display hex_digit_display_7 (.value(d_ff_32_q));  // open: dp
  Hex_Digit_Display hex_digit_display_8 (.value(d_ff_34_q));  // open: dp
  D_Flip_Flop d_ff_1 (.D(d_ff_23_q), .clk(clock_1_out), .Q(d_ff_1_q));  // open: Qn, preset, reset
  and and_1 (and_1_out, j_k_ff_14_q, j_k_ff_1_q);
  J_K_Flip_Flop j_k_ff_1 (
    .J(d_ff_1_q), .K(d_ff_1_q), .clk(d_ff_1_q), .Q(j_k_ff_1_q), .reset(and_17_out));  // open: Qn, preset
  D_Flip_Flop d_ff_2 (.D(j_k_ff_1_q), .clk(clock_1_out), .Q(d_ff_2_q[0]), .reset(button_3_out));  // open: Qn, preset
  and and_2 (and_2_out, and_1_out, d_ff_23_q);
  D_Flip_Flop d_ff_3 (.D(j_k_ff_1_q), .clk(d_ff_1_q), .Q(d_ff_3_q), .reset(button_3_out));  // open: Qn, preset
  D_Flip_Flop d_ff_4 (.D(and_2_out), .clk(clock_1_out), .Q(d_ff_4_q), .reset(button_3_out));  // open: Qn, preset
  and and_3 (and_3_out, j_k_ff_7_q, j_k_ff_2_q);
  and and_4 (and_4_out, j_k_ff_11_q, j_k_ff_2_q);
  J_K_Flip_Flop #(.trigger("falling")) j_k_ff_2 (
    .J(and_5_out), .K(and_5_out), .clk(clock_1_out), .Q(j_k_ff_2_q), .reset(and_3_out));  // open: Qn, preset
  D_Flip_Flop #(.trigger("falling")) d_ff_5 (
    .D(j_k_ff_2_q), .clk(clock_1_out), .Q(d_ff_15_q[3]), .reset(button_3_out));  // open: Qn, preset
  D_Flip_Flop d_ff_6 (.D(and_4_out), .clk(clock_1_out), .Q(d_ff_6_q));  // open: Qn, preset, reset
  J_K_Flip_Flop j_k_ff_3 (
    .J(d_ff_3_q), .K(d_ff_3_q), .clk(d_ff_3_q), .Q(j_k_ff_3_q), .reset(and_17_out));  // open: Qn, preset
  J_K_Flip_Flop j_k_ff_4 (
    .J(d_ff_4_q), .K(d_ff_4_q), .clk(d_ff_4_q), .Q(j_k_ff_4_q), .reset(and_18_out));  // open: Qn, preset
  and and_5 (and_5_out, and_10_out, j_k_ff_5_q);
  and and_6 (and_6_out, d_ff_6_q, j_k_ff_12_q);
  and and_7 (and_7_out, j_k_ff_8_q, j_k_ff_6_q);
  D_Flip_Flop d_ff_7 (.D(j_k_ff_3_q), .clk(clock_1_out), .Q(d_ff_2_q[1]), .reset(button_3_out));  // open: Qn, preset
  D_Flip_Flop d_ff_8 (.D(j_k_ff_4_q), .clk(clock_1_out), .Q(d_ff_8_q[0]), .reset(button_3_out));  // open: Qn, preset
  J_K_Flip_Flop #(.trigger("falling")) j_k_ff_5 (
    .J(and_10_out), .K(and_10_out), .clk(clock_1_out), .Q(j_k_ff_5_q), .reset(and_3_out));  // open: Qn, preset
  D_Flip_Flop #(.trigger("falling")) d_ff_9 (
    .D(j_k_ff_5_q), .clk(clock_1_out), .Q(d_ff_15_q[2]), .reset(button_3_out));  // open: Qn, preset
  and and_8 (and_8_out, and_6_out, j_k_ff_8_q);
  J_K_Flip_Flop #(.trigger("falling")) j_k_ff_6 (
    .J(and_8_out), .K(and_8_out), .clk(clock_1_out), .Q(j_k_ff_6_q), .reset(and_7_out));  // open: Qn, preset
  D_Flip_Flop #(.trigger("falling")) d_ff_10 (
    .D(j_k_ff_6_q), .clk(clock_1_out), .Q(d_ff_16_q[2]), .reset(button_3_out));  // open: Qn, preset
  and and_9 (and_9_out, j_k_ff_1_q, j_k_ff_3_q);
  D_Flip_Flop d_ff_11 (.D(and_9_out), .clk(d_ff_1_q), .Q(d_ff_11_q), .reset(button_3_out));  // open: Qn, preset
  D_Flip_Flop d_ff_12 (.D(j_k_ff_4_q), .clk(d_ff_4_q), .Q(d_ff_12_q), .reset(button_3_out));  // open: Qn, preset
  and and_10 (and_10_out, j_k_ff_11_q, j_k_ff_7_q);
  and and_11 (and_11_out, d_ff_6_q, j_k_ff_12_q);
  J_K_Flip_Flop #(.trigger("falling")) j_k_ff_7 (
    .J(j_k_ff_11_q), .K(j_k_ff_11_q), .clk(clock_1_out), .Q(j_k_ff_7_q), .reset(and_3_out));  // open: Qn, preset
  D_Flip_Flop #(.trigger("falling")) d_ff_13 (
    .D(j_k_ff_7_q), .clk(clock_1_out), .Q(d_ff_15_q[1]), .reset(button_3_out));  // open: Qn, preset
  J_K_Flip_Flop #(.trigger("falling")) j_k_ff_8 (
    .J(and_11_out), .K(and_11_out), .clk(clock_1_out), .Q(j_k_ff_8_q), .reset(and_7_out));  // open: Qn, preset
  D_Flip_Flop #(.trigger("falling")) d_ff_14 (
    .D(j_k_ff_8_q), .clk(clock_1_out), .Q(d_ff_16_q[1]), .reset(button_3_out));  // open: Qn, preset
  J_K_Flip_Flop j_k_ff_9 (
    .J(d_ff_11_q), .K(d_ff_11_q), .clk(d_ff_11_q), .Q(j_k_ff_9_q), .reset(and_17_out));  // open: Qn, preset
  J_K_Flip_Flop j_k_ff_10 (
    .J(d_ff_12_q), .K(d_ff_12_q), .clk(d_ff_12_q), .Q(j_k_ff_10_q), .reset(and_18_out));  // open: Qn, preset
  J_K_Flip_Flop #(.trigger("falling")) j_k_ff_11 (
    .J(t_ff_1_q), .K(t_ff_1_q), .clk(clock_1_out), .Q(j_k_ff_11_q), .reset(and_3_out));  // open: Qn, preset
  D_Flip_Flop #(.trigger("falling")) d_ff_15 (
    .D(j_k_ff_11_q), .clk(clock_1_out), .Q(d_ff_15_q[0]), .reset(button_3_out));  // open: Qn, preset
  J_K_Flip_Flop #(.trigger("falling")) j_k_ff_12 (
    .J(d_ff_6_q), .K(d_ff_6_q), .clk(clock_1_out), .Q(j_k_ff_12_q), .reset(and_7_out));  // open: Qn, preset
  D_Flip_Flop #(.trigger("falling")) d_ff_16 (
    .D(j_k_ff_12_q), .clk(clock_1_out), .Q(d_ff_16_q[0]), .reset(button_3_out));  // open: Qn, preset
  D_Flip_Flop d_ff_17 (.D(j_k_ff_9_q), .clk(clock_1_out), .Q(d_ff_2_q[2]), .reset(button_3_out));  // open: Qn, preset
  D_Flip_Flop d_ff_18 (.D(j_k_ff_10_q), .clk(clock_1_out), .Q(d_ff_8_q[1]), .reset(button_3_out));  // open: Qn, preset
  and and_12 (and_12_out, j_k_ff_1_q, j_k_ff_3_q, j_k_ff_9_q);
  and and_13 (and_13_out, j_k_ff_4_q, j_k_ff_10_q);
  D_Flip_Flop d_ff_19 (.D(and_13_out), .clk(d_ff_4_q), .Q(d_ff_19_q), .reset(button_3_out));  // open: Qn, preset
  Clock clock_1 (.out(clock_1_out));
  D_Flip_Flop #(.trigger("falling")) d_ff_20 (
    .D(clock_1_out), .clk(clock_1_out), .Q(d_ff_16_q[3]), .reset(button_3_out));  // open: Qn, preset
  D_Flip_Flop d_ff_21 (.D(and_12_out), .clk(d_ff_1_q), .Q(d_ff_21_q), .reset(button_3_out));  // open: Qn, preset
  J_K_Flip_Flop j_k_ff_13 (
    .J(d_ff_19_q), .K(d_ff_19_q), .clk(d_ff_19_q), .Q(j_k_ff_13_q), .reset(and_18_out));  // open: Qn, preset
  and and_14 (and_14_out, j_k_ff_6_q, j_k_ff_12_q);
  J_K_Flip_Flop j_k_ff_14 (
    .J(d_ff_21_q), .K(d_ff_21_q), .clk(d_ff_21_q), .Q(j_k_ff_14_q), .reset(and_17_out));  // open: Qn, preset
  D_Flip_Flop d_ff_22 (.D(j_k_ff_13_q), .clk(clock_1_out), .Q(d_ff_8_q[2]), .reset(button_3_out));  // open: Qn, preset
  D_Flip_Flop #(.trigger("falling")) d_ff_23 (
    .D(and_15_out), .clk(clock_1_out), .Q(d_ff_23_q));  // open: Qn, preset, reset
  and and_15 (and_15_out, d_ff_6_q, and_14_out);
  D_Flip_Flop d_ff_24 (.D(j_k_ff_14_q), .clk(clock_1_out), .Q(d_ff_2_q[3]), .reset(button_3_out));  // open: Qn, preset
  and and_16 (and_16_out, j_k_ff_4_q, j_k_ff_10_q, j_k_ff_13_q);
  D_Flip_Flop d_ff_25 (.D(and_16_out), .clk(d_ff_4_q), .Q(d_ff_25_q), .reset(button_3_out));  // open: Qn, preset
  and and_17 (and_17_out, j_k_ff_14_q, j_k_ff_3_q);
  D_Flip_Flop #(.trigger("falling")) d_ff_26 (
    .D(d_ff_15_q[3]), .clk(button_2_out), .Q(d_ff_34_q[3]), .reset(button_3_out));  // open: Qn, preset
  D_Flip_Flop #(.trigger("falling")) d_ff_27 (
    .D(d_ff_16_q[2]), .clk(button_2_out), .Q(d_ff_32_q[2]), .reset(button_3_out));  // open: Qn, preset
  J_K_Flip_Flop j_k_ff_15 (
    .J(d_ff_25_q), .K(d_ff_25_q), .clk(d_ff_25_q), .Q(j_k_ff_15_q), .reset(and_18_out));  // open: Qn, preset
  D_Flip_Flop #(.trigger("falling")) d_ff_28 (
    .D(d_ff_15_q[2]), .clk(button_2_out), .Q(d_ff_34_q[2]), .reset(button_3_out));  // open: Qn, preset
  D_Flip_Flop #(.trigger("falling")) d_ff_29 (
    .D(d_ff_16_q[1]), .clk(button_2_out), .Q(d_ff_32_q[1]), .reset(button_3_out));  // open: Qn, preset
  and and_18 (and_18_out, j_k_ff_15_q, j_k_ff_10_q);
  D_Flip_Flop d_ff_30 (.D(j_k_ff_15_q), .clk(clock_1_out), .Q(d_ff_8_q[3]), .reset(button_3_out));  // open: Qn, preset
  D_Flip_Flop #(.trigger("falling")) d_ff_31 (
    .D(d_ff_15_q[1]), .clk(button_2_out), .Q(d_ff_34_q[1]), .reset(button_3_out));  // open: Qn, preset
  D_Flip_Flop #(.trigger("falling")) d_ff_32 (
    .D(d_ff_16_q[0]), .clk(button_2_out), .Q(d_ff_32_q[0]), .reset(button_3_out));  // open: Qn, preset
  D_Flip_Flop d_ff_33 (
    .D(d_ff_2_q[0]), .clk(button_2_out), .Q(d_ff_33_q[0]), .reset(button_3_out));  // open: Qn, preset
  D_Flip_Flop #(.trigger("falling")) d_ff_34 (
    .D(d_ff_15_q[0]), .clk(button_2_out), .Q(d_ff_34_q[0]), .reset(button_3_out));  // open: Qn, preset
  D_Flip_Flop d_ff_35 (
    .D(d_ff_16_q[3]), .clk(button_2_out), .Q(d_ff_32_q[3]), .reset(button_3_out));  // open: Qn, preset
  D_Flip_Flop d_ff_36 (
    .D(d_ff_8_q[0]), .clk(button_2_out), .Q(d_ff_36_q[0]), .reset(button_3_out));  // open: Qn, preset
  D_Flip_Flop d_ff_37 (
    .D(d_ff_2_q[1]), .clk(button_2_out), .Q(d_ff_33_q[1]), .reset(button_3_out));  // open: Qn, preset
  D_Flip_Flop d_ff_38 (
    .D(d_ff_8_q[1]), .clk(button_2_out), .Q(d_ff_36_q[1]), .reset(button_3_out));  // open: Qn, preset
  D_Flip_Flop d_ff_39 (
    .D(d_ff_2_q[2]), .clk(button_2_out), .Q(d_ff_33_q[2]), .reset(button_3_out));  // open: Qn, preset
  D_Flip_Flop d_ff_40 (
    .D(d_ff_8_q[2]), .clk(button_2_out), .Q(d_ff_36_q[2]), .reset(button_3_out));  // open: Qn, preset
  D_Flip_Flop d_ff_41 (
    .D(d_ff_2_q[3]), .clk(button_2_out), .Q(d_ff_33_q[3]), .reset(button_3_out));  // open: Qn, preset
  D_Flip_Flop d_ff_42 (
    .D(d_ff_8_q[3]), .clk(button_2_out), .Q(d_ff_36_q[3]), .reset(button_3_out));  // open: Qn, preset

  // Notes on the sheet:
  //   Minutes
  //   Start / Stop
  //   Elapsed Time
  //   Seconds
  //   :
  //   Split
  //   Reset
  //   Minutes
  //   Clock Started
  //   Split Time
  //   :
  //   Seconds
endmodule
