// Logisim project stage2.circ as structural Verilog: 1 circuit, main circuit stage2
module stage2 (
);

  wire and_1_out, and_2_out, and_3_out, button_1_out, clock_1_out, j_k_ff_1_q, j_k_ff_2_q, j_k_ff_3_q,
       j_k_ff_4_q, t_ff_1_q;
  wire [3:0] d_ff_4_q;

  Hex_Digit_Display hex_digit_display_1 ();  // open: value, dp
  Hex_Digit_Display hex_digit_display_2 ();  // open: value, dp
  Button button_1 (.out(button_1_out));
  Hex_Digit_Display hex_digit_display_3 ();  // open: value, dp
  Button button_2 ();  // open: out
  Hex_Digit_Display hex_digit_display_4 (.value(d_ff_4_q));  // open: dp
  Button button_3 ();  // open: out
  Hex_Digit_Display hex_digit_display_5 ();  // open: value, dp
  LED led_1 (.in(t_ff_1_q));
  T_Flip_Flop t_ff_1 (.T(button_1_out), .clk(button_1_out), .Q(t_ff_1_q));  // open: Qn, reset, preset
  Hex_Digit_Display hex_digit_display_6 ();  // open: value, dp
  Hex_Digit_Display hex_digit_display_7 ();  // open: value, dp
  Hex_Digit_Display hex_digit_display_8 ();  // open: value, dp
  and and_1 (and_1_out, j_k_ff_3_q, j_k_ff_1_q);
  and and_2 (and_2_out, and_3_out, j_k_ff_2_q);
  J_K_Flip_Flop #(.trigger("falling")) j_k_ff_1 (
    .J(and_2_out), .K(and_2_out), .clk(clock_1_out), .Q(j_k_ff_1_q), .reset(and_1_out));  // open: Qn, preset
  D_Flip_Flop #(.trigger("falling")) d_ff_1 (
    .D(j_k_ff_1_q), .clk(clock_1_out), .Q(d_ff_4_q[3]));  // open: Qn, preset, reset
  and and_3 (and_3_out, j_k_ff_4_q, j_k_ff_3_q);
  J_K_Flip_Flop #(.trigger("falling")) j_k_ff_2 (
    .J(and_3_out), .K(and_3_out), .clk(clock_1_out), .Q(j_k_ff_2_q), .reset(and_1_out));  // open: Qn, preset
  D_Flip_Flop #(.trigger("falling")) d_ff_2 (
    .D(j_k_ff_2_q), .clk(clock_1_out), .Q(d_ff_4_q[2]));  // open: Qn, preset, reset
  J_K_Flip_Flop #(.trigger("falling")) j_k_ff_3 (
    .J(j_k_ff_4_q), .K(j_k_ff_4_q), .clk(clock_1_out), .Q(j_k_ff_3_q), .reset(and_1_out));  // open: Qn, preset
  D_Flip_Flop #(.trigger("falling")) d_ff_3 (
    .D(j_k_ff_3_q), .clk(clock_1_out), .Q(d_ff_4_q[1]));  // open: Qn, preset, reset
  J_K_Flip_Flop #(.trigger("falling")) j_k_ff_4 (
    .J(t_ff_1_q), .K(t_ff_1_q), .clk(clock_1_out), .Q(j_k_ff_4_q), .reset(and_1_out));  // open: Qn, preset
  D_Flip_Flop #(.trigger("falling")) d_ff_4 (
    .D(j_k_ff_4_q), .clk(clock_1_out), .Q(d_ff_4_q[0]));  // open: Qn, preset, reset
  Clock clock_1 (.out(clock_1_out));

  // Notes on the sheet:
  //   Minutes
  //   Start / Stop
  //   Elapsed Time
  //   Seconds
  //   :
  //   Split
  //   Reset
  //   Minutes
  //   Clock Started
  //   Split Time
  //   :
  //   Seconds
endmodule
