// Logisim project stage3.circ as structural Verilog: 1 circuit, main circuit stage3
module stage3 (
);

  wire and_1_out, and_2_out, and_3_out, and_4_out, and_5_out, and_6_out, and_7_out, and_8_out, button_1_out,
       button_3_out, clock_1_out, d_ff_2_q, j_k_ff_1_q, j_k_ff_2_q, j_k_ff_3_q, j_k_ff_4_q, j_k_ff_5_q,
       j_k_ff_6_q, j_k_ff_7_q, t_ff_1_q;
  wire [3:0] d_ff_7_q, d_ff_8_q;

  Hex_Digit_Display hex_digit_display_1 ();  // open: value, dp
  Hex_Digit_Display hex_digit_display_2 ();  // open: value, dp
  Button button_1 (.out(button_1_out));
  Hex_Digit_Display hex_digit_display_3 (.value(d_ff_8_q));  // open: dp
  Button button_2 ();  // open: out
  Hex_Digit_Display hex_digit_display_4 (.value(d_ff_7_q));  // open: dp
  Button button_3 (.out(button_3_out));
  Hex_Digit_Display hex_digit_display_5 ();  // open: value, dp
  LED led_1 (.in(t_ff_1_q));
  T_Flip_Flop t_ff_1 (.T(button_1_out), .clk(button_1_out), .Q(t_ff_1_q), .reset(button_3_out));  // open: Qn, preset
  Hex_Digit_Display hex_digit_display_6 ();  // open: value, dp
  Hex_Digit_Display hex_digit_display_7 ();  // open: value, dp
  Hex_Digit_Display hex_digit_display_8 ();  // open: value, dp
  and and_1 (and_1_out, j_k_ff_4_q, j_k_ff_1_q);
  and and_2 (and_2_out, j_k_ff_6_q, j_k_ff_1_q);
  J_K_Flip_Flop #(.trigger("falling")) j_k_ff_1 (
    .J(and_3_out), .K(and_3_out), .clk(clock_1_out), .Q(j_k_ff_1_q), .reset(and_1_out));  // open: Qn, preset
  D_Flip_Flop #(.trigger("falling")) d_ff_1 (
    .D(j_k_ff_1_q), .clk(clock_1_out), .Q(d_ff_7_q[3]), .reset(button_3_out));  // open: Qn, preset
  D_Flip_Flop d_ff_2 (.D(and_2_out), .clk(clock_1_out), .Q(d_ff_2_q), .reset(button_3_out));  // open: Qn, preset
  and and_3 (and_3_out, and_7_out, j_k_ff_2_q);
  and and_4 (and_4_out, d_ff_2_q, j_k_ff_7_q);
  and and_5 (and_5_out, j_k_ff_5_q, j_k_ff_3_q);
  J_K_Flip_Flop #(.trigger("falling")) j_k_ff_2 (
    .J(and_7_out), .K(and_7_out), .clk(clock_1_out), .Q(j_k_ff_2_q), .reset(and_1_out));  // open: Qn, preset
  D_Flip_Flop #(.trigger("falling")) d_ff_3 (
    .D(j_k_ff_2_q), .clk(clock_1_out), .Q(d_ff_7_q[2]), .reset(button_3_out));  // open: Qn, preset
  and and_6 (and_6_out, and_4_out, j_k_ff_5_q);
  J_K_Flip_Flop #(.trigger("falling")) j_k_ff_3 (
    .J(and_6_out), .K(and_6_out), .clk(clock_1_out), .Q(j_k_ff_3_q), .reset(and_5_out));  // open: Qn, preset
  D_Flip_Flop #(.trigger("falling")) d_ff_4 (
    .D(j_k_ff_3_q), .clk(clock_1_out), .Q(d_ff_8_q[2]), .reset(button_3_out));  // open: Qn, preset
  and and_7 (and_7_out, j_k_ff_6_q, j_k_ff_4_q);
  and and_8 (and_8_out, d_ff_2_q, j_k_ff_7_q);
  J_K_Flip_Flop #(.trigger("falling")) j_k_ff_4 (
    .J(j_k_ff_6_q), .K(j_k_ff_6_q), .clk(clock_1_out), .Q(j_k_ff_4_q), .reset(and_1_out));  // open: Qn, preset
  D_Flip_Flop #(.trigger("falling")) d_ff_5 (
    .D(j_k_ff_4_q), .clk(clock_1_out), .Q(d_ff_7_q[1]), .reset(button_3_out));  // open: Qn, preset
  J_K_Flip_Flop #(.trigger("falling")) j_k_ff_5 (
    .J(and_8_out), .K(and_8_out), .clk(clock_1_out), .Q(j_k_ff_5_q), .reset(and_5_out));  // open: Qn, preset
  D_Flip_Flop #(.trigger("falling")) d_ff_6 (
    .D(j_k_ff_5_q), .clk(clock_1_out), .Q(d_ff_8_q[1]), .reset(button_3_out));  // open: Qn, preset
  J_K_Flip_Flop #(.trigger("falling")) j_k_ff_6 (
    .J(t_ff_1_q), .K(t_ff_1_q), .clk(clock_1_out), .Q(j_k_ff_6_q), .reset(and_1_out));  // open: Qn, preset
  D_Flip_Flop #(.trigger("falling")) d_ff_7 (
    .D(j_k_ff_6_q), .clk(clock_1_out), .Q(d_ff_7_q[0]), .reset(button_3_out));  // open: Qn, preset
  J_K_Flip_Flop #(.trigger("falling")) j_k_ff_7 (
    .J(d_ff_2_q), .K(d_ff_2_q), .clk(clock_1_out), .Q(j_k_ff_7_q), .reset(and_5_out));  // open: Qn, preset
  D_Flip_Flop #(.trigger("falling")) d_ff_8 (
    .D(j_k_ff_7_q), .clk(clock_1_out), .Q(d_ff_8_q[0]), .reset(button_3_out));  // open: Qn, preset
  Clock clock_1 (.out(clock_1_out));
  D_Flip_Flop #(.trigger("falling")) d_ff_9 (
    .D(clock_1_out), .clk(clock_1_out), .Q(d_ff_8_q[3]), .reset(button_3_out));  // open: Qn, preset

  // Notes on the sheet:
  //   Minutes
  //   Start / Stop
  //   Elapsed Time
  //   Seconds
  //   :
  //   Split
  //   Reset
  //   Minutes
  //   Clock Started
  //   Split Time
  //   :
  //   Seconds
endmodule
